# Fritzing sketch 1.a.i.11_voltage-regulation (saved by Fritzing 0.9.0b)
breadboards: 1

parts:
  U1 = LIPO-2000mAh [package=lipo-2000]
  U5 = SPX29302 [package=q5-dd_spx29300]  # not connected
  U6 = LM3480IM4 [package=sot23-3]  # not connected
  U7 = LM3480IM4 [package=sot23-3]

nets:
  N1: U1.+, U7.IN
  N2: U1.-, U7.GND

notes:
  12V
  5V
  5V step-down
  5V step-up
  variable voltage regulator
  Touch to VOUT
