# Fritzing sketch 1.a.i.6_led-current-limiter (saved by Fritzing 0.9.0b)
breadboards: 1

parts:
  LED1 = LEDs [package=led10mm]
  U1 = POT [package=3362u]

nets:
  N1: LED1.C, U1.S

notes:
  5V
  200Ω
